# Fritzing sketch ZHSG (saved by Fritzing 0.8.7b)
circuit board: 7.15341cm x 5.52969cm
breadboards: 1

parts:
  Arduino = Arduino Uno (Rev3)
  LCD1 = LCD screen
  R2 = Resistor [tolerance=±5% resistance=1.5k package=THT]
  R4 = Resistor [tolerance=±5% resistance=1.5k package=THT]
  LM4040CIZ-5_0-NOPB = TRANSISTOR_NPN [package=to-92]
  R5 = Resistor [tolerance=±5% resistance=540 package=THT]
  R6 = Resistor [tolerance=±5% resistance=22k package=THT]
  R7 = Resistor [tolerance=±5% resistance=47k package=THT]
  R8 = Resistor [tolerance=±5% resistance=22k package=THT]
  R9 = Resistor [tolerance=±5% resistance=47k package=THT]
  R10 = Resistor [tolerance=±5% resistance=1k package=THT]
  R11 = Resistor [tolerance=±5% resistance=1k package=THT]
  Q1 = MOSFET-NCHANNEL [package=to-92]
  R12 = Trimmer Potentiometer [maximum_resistance=10kΩ package=THT]
  R14 = Resistor [tolerance=±5% resistance=100k package=THT]
  R15 = Resistor [tolerance=±5% resistance=220 package=THT]
  R16 = Resistor [tolerance=±5% resistance=100 package=THT]
  R17 = Trimmer Potentiometer [maximum_resistance=10kΩ package=THT]
  J2 = longpad pin header, 2 pins [form="long pad"]
  Q2 = NPN-Transistor [package="TO92 [THT]"]
  R18 = Resistor [tolerance=±5% resistance=4.7k package=THT]
  U4 = Voltage Regulator - 5V [package="TO220 [THT]"]
  C3 = Electrolytic Capacitor [capacitance=4.7µF package="100 mil [THT, electrolytic]"]
  C4 = Electrolytic Capacitor [capacitance=4.7µF package="100 mil [THT, electrolytic]"]
  L2 = Inductor [inductance=8.7 current=1.5 package="400 mil [THT]"]
  U2 = TLP621 [package=THT]
  U1 = TLP621 [package=THT]
  U5 = TLP621 [package=THT]
  R19 = Resistor [tolerance=±5% resistance=1k package=THT]
  R20 = Resistor [tolerance=±5% resistance=1.5k package=THT]
  IN = screw terminal, 8 pins
  R13 = Trimmer Potentiometer [maximum_resistance=10kΩ package=THT]
  R21 = Resistor [tolerance=±5% resistance=100k package=THT]
  J1 = longpad pin header, 8 pins [form="long pad"]
  Out = Screw terminal - 2 pins [package=THT]
  ENCODER1 = Rotary Encoder with Knob
  R22 = Resistor [tolerance=±5% resistance=4.7k package=THT]
  R23 = Resistor [tolerance=±5% resistance=4.7k package=THT]
  C5 = Ceramic Capacitor [capacitance=10nF package="100 mil [THT, multilayer]"]
  C6 = Ceramic Capacitor [capacitance=10nF package="100 mil [THT, multilayer]"]
  R24 = Resistor [tolerance=±5% resistance=82k package=THT]
  R25 = Resistor [tolerance=±5% resistance=82k package=THT]
  R26 = Resistor [tolerance=±5% resistance=10k package=THT]
  J4 = female pin header, 12 pins [form="♀ (female)"]  # not connected
  J3 = male pin header, 12 pins [form="♂ (male)"]  # not connected

nets:
  N1: Arduino.A0, R6.Pin_1, R7.Pin_0
  N2: Arduino.A1, R8.Pin_1, R9.Pin_0
  N3: Arduino.A2, IN.pin7, J1.pin7
  N4: Arduino.D8, Q1.G, R14.Pin_0
  N5: Arduino.D9_PWM, R18.Pin_0
  N6: Arduino.D10_PWM/SS, ENCODER1.no_name_yet#4, R26.Pin_1
  N7: Arduino.D11_PWM/MOSI, U5.Pin_4, R20.Pin_1
  N8: Arduino.D12/MISO, R4.Pin_1, U2.Pin_4
  N9: Arduino.D13/SCK, R2.Pin_1, U1.Pin_4
  GND: Arduino.GND, LCD1.VSS, LCD1.R/W, LCD1.LED-, LM4040CIZ-5_0-NOPB.E, R12.wiper, R14.Pin_1, R15.Pin_1, R17.leg1, U4.GND, C3.-, C4.-, U2.Pin_2, U2.Pin_3, U1.Pin_2, U1.Pin_3, U5.Pin_2, U5.Pin_3, IN.pin8, R13.wiper, R21.Pin_1, J1.pin8, ENCODER1.no_name_yet#3, C5.0, C6.0, R26.Pin_0
  N10: Arduino.AREF, LM4040CIZ-5_0-NOPB.B, R5.Pin_1
  N11: Arduino.D0/RX, C5.1, R24.Pin_0
  N12: Arduino.D1/TX, C6.1, R25.Pin_0
  N13: Arduino.D2, LCD1.RS
  N14: Arduino.D3_PWM, LCD1.E
  N15: Arduino.D4, LCD1.DB4
  N16: Arduino.D5_PWM, LCD1.DB5
  N17: Arduino.D6_PWM, LCD1.DB6
  N18: Arduino.D7, LCD1.DB7
  5V: Arduino.5V, LCD1.VDD, R2.Pin_0, R4.Pin_0, R5.Pin_0, R17.leg2, U4.output_voltage, R20.Pin_0, ENCODER1.no_name_yet#5, R22.Pin_1, R23.Pin_1
  N19: LCD1.V0, R17.wiper
  N20: LCD1.LED+, R15.Pin_0, R16.Pin_0
  14V: R6.Pin_0, IN.pin2, J1.pin2
  N21: R7.Pin_1, R12.leg2
  12V: R8.Pin_0, Q1.D, Q2.C, C4.+, L2.pin_0, IN.pin1, J1.pin1
  N22: R9.Pin_1, R13.leg2
  N23: R10.Pin_0, IN.pin5, J1.pin5
  N24: R10.Pin_1, U1.Pin_1
  N25: R11.Pin_0, IN.pin4, J1.pin4
  N26: R11.Pin_1, U2.Pin_1
  N27: Q1.S, J2.pin1, Out.pin1
  16V: R16.Pin_1, IN.pin6, J1.pin6
  N28: J2.pin2, Q2.E, R21.Pin_0, Out.pin2
  N29: Q2.B, R18.Pin_1
  N30: U4.input_voltage, C3.+, L2.pin_1
  N31: U5.Pin_1, R19.Pin_1
  N32: R19.Pin_0, IN.pin3, J1.pin3
  N33: ENCODER1.no_name_yet#1, R22.Pin_0, R24.Pin_1
  N34: ENCODER1.no_name_yet#2, R23.Pin_0, R25.Pin_1

notes:
  Spannungsmessung Batt. 1
  Spannungsmessung Batt. 2
  12 V Zweitbatterie
  GND
  Zündung
  Zuheizer
  12 V Hauptbatterie
  Trennrelais +
  Amaturenbel
  4,5V / 45mA
  Debug Inputs
  Temp Kühlwasser
  Spannungsreferenz
  Vcc
  Pin 8 GND
  Pin 7 Temp Kühlwasser
  Pin 6 Amaturenbeleuchtung
  Pin 5 Kl 15a Zündung
  Pin 4 Zuheizer Uhr
  Pin 3 Steuerung ZH von Board Elek
  Pin 2 12V Hauptbatterie
  Pin 1 12V Zweitbatterie
  Zuheizer +
  +Sek
  +Pri
  xxx
  ZH Uhr
  Kl15a
  Temp
  Kl58b
  Relais+
  ZH

custom parts:
  Rotary Encoder with Knob: Rotary Encoder with 1/4" Shaft and Knob
